# Fritzing sketch Frizing_diagrama (saved by Fritzing 0.9.0b)
breadboards: 1

parts:
  U1 = ESP8266 WiFi Module [part_number=ESP8266]
  Parte1 = FTDI Basic Programmer
  Parte2 = Arduino Uno (Rev3) - ICSP

nets:
  N1: U1.RXD, Parte1.TXO
  VCC: U1.VCC, Parte2.3V3
  N2: U1.TXD, Parte1.RXI
  GND: Parte1.GND, Parte2.GND

custom parts:
  ESP8266 WiFi Module: Generic WiFi Module based on the ESP8266 with onboard PCB antenna and UART communications
